# Fritzing sketch RGBControledSerial (saved by Fritzing 0.9.0b)
breadboards: 1

parts:
  LED1 = RGB LED (com. anode, rbg) [package="5 mm [THT]"]
  Part1 = Arduino Uno (Rev3)
  R1 = Resistor [tolerance=±5% resistance=220 package=THT]  # not connected
  R2 = Resistor [tolerance=±5% resistance=220 package=THT]
  R3 = Resistor [tolerance=±5% resistance=220 package=THT]

nets:
  N1: LED1.common_anode, Part1.GND
  N2: LED1.blue_cathode, R2.Pin_0
  N3: LED1.green_cathode, R3.Pin_0
  N4: Part1.D11_PWM/MOSI, R3.Pin_1
  N5: Part1.D12/MISO, R2.Pin_1

notes:
  RGB Led Controled via Serial Comm from PC
